// Digital circuit 2s-complement_4bits.dig as structural Verilog
module _2s_complement_4bits (
  input  A0,
  input  A1_2,
  input  A2_2,
  input  A3_2,
  output A3,
  output A2,
  output A1,
  output A0_2,
  output cout_restant_apres_les__ajouts_de_1
);

  wire half_adder_1bit_1_cout, half_adder_1bit_2_cout, half_adder_1bit_3_cout, not_1_out, not_2_out,
       not_3_out, not_4_out;

  not not_1 (not_1_out, A3_2);
  not not_2 (not_2_out, A2_2);
  not not_3 (not_3_out, A1_2);
  not not_4 (not_4_out, A0);
  half_adder_1bit half_adder_1bit_1 (.A(not_4_out), .B(1'b1), .S(A0_2), .Cout(half_adder_1bit_1_cout));
  half_adder_1bit half_adder_1bit_2 (.A(not_3_out), .B(half_adder_1bit_1_cout), .S(A1), .Cout(half_adder_1bit_2_cout));
  half_adder_1bit half_adder_1bit_3 (.A(not_2_out), .B(half_adder_1bit_2_cout), .S(A2), .Cout(half_adder_1bit_3_cout));
  half_adder_1bit half_adder_1bit_4 (
    .A(not_1_out), .B(half_adder_1bit_3_cout), .S(A3), .Cout(cout_restant_apres_les__ajouts_de_1));
endmodule
