// Digital circuit full-adder_1bit.dig as structural Verilog
module full_adder_1bit (
  input  Input0,
  output BCD0
);

  // LUT #(.Bits(4), .Function("(votre fonction de conversion ici)")) lut_1: pin names not known; wires that end beside it: Input0, BCD0
endmodule
