// Digital circuit full-adder_4bits.dig as structural Verilog
module full_adder_4bits (
  input  A0,
  input  B3,
  input  Cin,
  input  A1,
  input  A2,
  input  A3,
  input  B2,
  input  B1,
  input  B0,
  output S3,
  output Cout,
  output S2,
  output S1,
  output S0
);

  wire full_adder_1bit_1_p3, full_adder_1bit_1_p5, full_adder_1bit_2_p5;

  // full_adder_1bit full_adder_1bit_1: pin names not known; wires that end beside it: A2, B2, full_adder_1bit_1_p3, S2, full_adder_1bit_1_p5
  // full_adder_1bit full_adder_1bit_2: pin names not known; wires that end beside it: A0, B0, Cin, S0, full_adder_1bit_2_p5
  // full_adder_1bit full_adder_1bit_3: pin names not known; wires that end beside it: A1, B1, full_adder_1bit_2_p5, S1, full_adder_1bit_1_p3
  // full_adder_1bit full_adder_1bit_4: pin names not known; wires that end beside it: A3, B3, full_adder_1bit_1_p5, S3, Cout
endmodule

/* Test case:
Cin A3 A2 A1 A0 B3 B2 B1 B0 Cout S3 S2 S1 S0
loop(A,16)
  loop(B,16)
    0 bits(4,A) bits(4,B) bits(5,A+B)
    1 bits(4,A) bits(4,B) bits(5,A+B+1)
  end loop
end loop
*/
