// Digital circuit afficheur_bin_2_7seg_4bits.dig as structural Verilog
module afficheur_bin_2_7seg_4bits (
  input  BIN0,
  input  BIN1,
  input  BIN2,
  input  BIN3
);

  wire conv_bin_2_7seg_4bits_1_a0, conv_bin_2_7seg_4bits_1_a1, conv_bin_2_7seg_4bits_1_b0,
       conv_bin_2_7seg_4bits_1_b1, conv_bin_2_7seg_4bits_1_c0, conv_bin_2_7seg_4bits_1_c1,
       conv_bin_2_7seg_4bits_1_d0, conv_bin_2_7seg_4bits_1_d1, conv_bin_2_7seg_4bits_1_e0,
       conv_bin_2_7seg_4bits_1_e1, conv_bin_2_7seg_4bits_1_f0, conv_bin_2_7seg_4bits_1_f1,
       conv_bin_2_7seg_4bits_1_g0, conv_bin_2_7seg_4bits_1_g1;

  conv_bin_2_7seg_4bits conv_bin_2_7seg_4bits_1 (
    .BIN0(BIN0), .BIN1(BIN1), .BIN2(BIN2), .BIN3(BIN3), .A0(conv_bin_2_7seg_4bits_1_a0),
    .B0(conv_bin_2_7seg_4bits_1_b0), .C0(conv_bin_2_7seg_4bits_1_c0), .D0(conv_bin_2_7seg_4bits_1_d0),
    .E0(conv_bin_2_7seg_4bits_1_e0), .F0(conv_bin_2_7seg_4bits_1_f0), .G0(conv_bin_2_7seg_4bits_1_g0),
    .A1(conv_bin_2_7seg_4bits_1_a1), .B1(conv_bin_2_7seg_4bits_1_b1), .C1(conv_bin_2_7seg_4bits_1_c1),
    .D1(conv_bin_2_7seg_4bits_1_d1), .E1(conv_bin_2_7seg_4bits_1_e1), .F1(conv_bin_2_7seg_4bits_1_f1),
    .G1(conv_bin_2_7seg_4bits_1_g1));
  Seven_Seg seven_seg_1 (
    .a(conv_bin_2_7seg_4bits_1_a0), .b(conv_bin_2_7seg_4bits_1_b0), .c(conv_bin_2_7seg_4bits_1_c0),
    .d(conv_bin_2_7seg_4bits_1_d0), .e(conv_bin_2_7seg_4bits_1_e0), .f(conv_bin_2_7seg_4bits_1_f0),
    .g(conv_bin_2_7seg_4bits_1_g0), .dp(1'b0));
  Seven_Seg seven_seg_2 (
    .a(conv_bin_2_7seg_4bits_1_a1), .b(conv_bin_2_7seg_4bits_1_b1), .c(conv_bin_2_7seg_4bits_1_c1),
    .d(conv_bin_2_7seg_4bits_1_d1), .e(conv_bin_2_7seg_4bits_1_e1), .f(conv_bin_2_7seg_4bits_1_f1),
    .g(conv_bin_2_7seg_4bits_1_g1), .dp(1'b0));
endmodule
