// Digital circuit afficheur_bin_2_7seg_8bits.dig as structural Verilog
module afficheur_bin_2_7seg_8bits (
  input  BIN0,
  input  BIN1,
  input  BIN2,
  input  BIN3,
  input  BIN4,
  input  BIN5,
  input  BIN6,
  input  BIN7
);

  wire conv_bin_2_7seg_8bits_1_a0, conv_bin_2_7seg_8bits_1_a1, conv_bin_2_7seg_8bits_1_a2,
       conv_bin_2_7seg_8bits_1_b0, conv_bin_2_7seg_8bits_1_b1, conv_bin_2_7seg_8bits_1_b2,
       conv_bin_2_7seg_8bits_1_c0, conv_bin_2_7seg_8bits_1_c1, conv_bin_2_7seg_8bits_1_c2,
       conv_bin_2_7seg_8bits_1_d0, conv_bin_2_7seg_8bits_1_d1, conv_bin_2_7seg_8bits_1_d2,
       conv_bin_2_7seg_8bits_1_e0, conv_bin_2_7seg_8bits_1_e1, conv_bin_2_7seg_8bits_1_e2,
       conv_bin_2_7seg_8bits_1_f0, conv_bin_2_7seg_8bits_1_f1, conv_bin_2_7seg_8bits_1_f2,
       conv_bin_2_7seg_8bits_1_g0, conv_bin_2_7seg_8bits_1_g1, conv_bin_2_7seg_8bits_1_g2;

  conv_bin_2_7seg_8bits conv_bin_2_7seg_8bits_1 (
    .BIN0(BIN0), .BIN1(BIN1), .BIN2(BIN2), .BIN3(BIN3), .BIN4(BIN4), .BIN5(BIN5), .BIN6(BIN6), .BIN7(BIN7),
    .A0(conv_bin_2_7seg_8bits_1_a0), .B0(conv_bin_2_7seg_8bits_1_b0), .C0(conv_bin_2_7seg_8bits_1_c0),
    .D0(conv_bin_2_7seg_8bits_1_d0), .E0(conv_bin_2_7seg_8bits_1_e0), .F0(conv_bin_2_7seg_8bits_1_f0),
    .G0(conv_bin_2_7seg_8bits_1_g0), .A1(conv_bin_2_7seg_8bits_1_a1), .B1(conv_bin_2_7seg_8bits_1_b1),
    .C1(conv_bin_2_7seg_8bits_1_c1), .D1(conv_bin_2_7seg_8bits_1_d1), .E1(conv_bin_2_7seg_8bits_1_e1),
    .F1(conv_bin_2_7seg_8bits_1_f1), .G1(conv_bin_2_7seg_8bits_1_g1), .A2(conv_bin_2_7seg_8bits_1_a2),
    .B2(conv_bin_2_7seg_8bits_1_b2), .C2(conv_bin_2_7seg_8bits_1_c2), .D2(conv_bin_2_7seg_8bits_1_d2),
    .E2(conv_bin_2_7seg_8bits_1_e2), .F2(conv_bin_2_7seg_8bits_1_f2), .G2(conv_bin_2_7seg_8bits_1_g2));
  Seven_Seg seven_seg_1 (
    .a(conv_bin_2_7seg_8bits_1_a2), .b(conv_bin_2_7seg_8bits_1_b2), .c(conv_bin_2_7seg_8bits_1_c2),
    .d(conv_bin_2_7seg_8bits_1_d2), .e(conv_bin_2_7seg_8bits_1_e2), .f(conv_bin_2_7seg_8bits_1_f2),
    .g(conv_bin_2_7seg_8bits_1_g2), .dp(1'b1));
  Seven_Seg seven_seg_2 (
    .a(conv_bin_2_7seg_8bits_1_a1), .b(conv_bin_2_7seg_8bits_1_b1), .c(conv_bin_2_7seg_8bits_1_c1),
    .d(conv_bin_2_7seg_8bits_1_d1), .e(conv_bin_2_7seg_8bits_1_e1), .f(conv_bin_2_7seg_8bits_1_f1),
    .g(conv_bin_2_7seg_8bits_1_g1), .dp(1'b1));
  Seven_Seg seven_seg_3 (
    .a(conv_bin_2_7seg_8bits_1_a0), .b(conv_bin_2_7seg_8bits_1_b0), .c(conv_bin_2_7seg_8bits_1_c0),
    .d(conv_bin_2_7seg_8bits_1_d0), .e(conv_bin_2_7seg_8bits_1_e0), .f(conv_bin_2_7seg_8bits_1_f0),
    .g(conv_bin_2_7seg_8bits_1_g0), .dp(1'b1));
endmodule
