// Digital circuit conv_bcd_2_7seg_4bits.dig as structural Verilog
module conv_bcd_2_7seg_4bits (
  input  B0,
  input  B1,
  input  B2,
  input  B3,
  output A,
  output B,
  output C,
  output D,
  output E,
  output F,
  output G
);

  LookUpTable #(.Bits(7)) LUT_7seg (.in0(B0), .in1(B1), .in2(B2), .in3(B3), .out({G, F, E, D, C, B, A}));

  // Notes on the sheet:
  //   contents of LUT_7seg (hex, n*v repeats v):
  //   3f,6,5b,4f,66,6d,7d,7,7f,6f
endmodule
