// Digital circuit conv_bin_2_7seg_4bits.dig as structural Verilog
module conv_bin_2_7seg_4bits (
  input  BIN0,
  input  BIN1,
  input  BIN2,
  input  BIN3,
  output A0,
  output B0,
  output C0,
  output D0,
  output E0,
  output F0,
  output G0,
  output A1,
  output B1,
  output C1,
  output D1,
  output E1,
  output F1,
  output G1
);

  wire conv_bin_2_bcd_4bits_1_s0, conv_bin_2_bcd_4bits_1_s1, conv_bin_2_bcd_4bits_1_s2,
       conv_bin_2_bcd_4bits_1_s3, conv_bin_2_bcd_4bits_1_s4;

  conv_bin_2_bcd_4bits conv_bin_2_bcd_4bits_1 (
    .BIN0(BIN0), .BIN1(BIN1), .BIN2(BIN2), .BIN3(BIN3), .S0(conv_bin_2_bcd_4bits_1_s0),
    .S1(conv_bin_2_bcd_4bits_1_s1), .S2(conv_bin_2_bcd_4bits_1_s2), .S3(conv_bin_2_bcd_4bits_1_s3),
    .S4(conv_bin_2_bcd_4bits_1_s4));
  conv_bcd_2_7seg_4bits conv_bcd_2_7seg_4bits_1 (
    .B0(conv_bin_2_bcd_4bits_1_s0), .B1(conv_bin_2_bcd_4bits_1_s1), .B2(conv_bin_2_bcd_4bits_1_s2),
    .B3(conv_bin_2_bcd_4bits_1_s3), .A(A0), .B(B0), .C(C0), .D(D0), .E(E0), .F(F0), .G(G0));
  conv_bcd_2_7seg_4bits conv_bcd_2_7seg_4bits_2 (
    .B0(conv_bin_2_bcd_4bits_1_s4), .B1(1'b0), .B2(1'b0), .B3(1'b0), .A(A1), .B(B1), .C(C1), .D(D1), .E(E1),
    .F(F1), .G(G1));
endmodule
