// Digital circuit conv_bin_2_7seg_8bits.dig as structural Verilog
module conv_bin_2_7seg_8bits (
  input  BIN0,
  input  BIN1,
  input  BIN2,
  input  BIN3,
  input  BIN4,
  input  BIN5,
  input  BIN6,
  input  BIN7,
  output A0,
  output B0,
  output C0,
  output D0,
  output E0,
  output F0,
  output G0,
  output A1,
  output B1,
  output C1,
  output D1,
  output E1,
  output F1,
  output G1,
  output A2,
  output B2,
  output C2,
  output D2,
  output E2,
  output F2,
  output G2
);

  wire conv_bin_2_bcd_8bits_1_p10, conv_bin_2_bcd_8bits_1_p11, conv_bin_2_bcd_8bits_1_p12,
       conv_bin_2_bcd_8bits_1_p13, conv_bin_2_bcd_8bits_1_p14, conv_bin_2_bcd_8bits_1_p15,
       conv_bin_2_bcd_8bits_1_p16, conv_bin_2_bcd_8bits_1_p17, conv_bin_2_bcd_8bits_1_p18,
       conv_bin_2_bcd_8bits_1_p19, conv_bin_2_bcd_8bits_1_p20, conv_bin_2_bcd_8bits_1_p21;

  // conv_bin_2_bcd_8bits conv_bin_2_bcd_8bits_1: pin names not known; wires that end beside it: BIN0, BIN1, BIN2, BIN3, BIN4, BIN5, BIN6, BIN7, 1'b1, conv_bin_2_bcd_8bits_1_p10, conv_bin_2_bcd_8bits_1_p11, conv_bin_2_bcd_8bits_1_p12, conv_bin_2_bcd_8bits_1_p13, conv_bin_2_bcd_8bits_1_p14, conv_bin_2_bcd_8bits_1_p15, conv_bin_2_bcd_8bits_1_p16, conv_bin_2_bcd_8bits_1_p17, conv_bin_2_bcd_8bits_1_p18, conv_bin_2_bcd_8bits_1_p19, conv_bin_2_bcd_8bits_1_p20, conv_bin_2_bcd_8bits_1_p21
  conv_bcd_2_7seg_4bits conv_bcd_2_7seg_4bits_1 (
    .B0(conv_bin_2_bcd_8bits_1_p10), .B1(conv_bin_2_bcd_8bits_1_p11), .B2(conv_bin_2_bcd_8bits_1_p12),
    .B3(conv_bin_2_bcd_8bits_1_p13), .A(A0), .B(B0), .C(C0), .D(D0), .E(E0), .F(F0), .G(G0));
  conv_bcd_2_7seg_4bits conv_bcd_2_7seg_4bits_2 (
    .B0(conv_bin_2_bcd_8bits_1_p18), .B1(conv_bin_2_bcd_8bits_1_p19), .B2(conv_bin_2_bcd_8bits_1_p20),
    .B3(conv_bin_2_bcd_8bits_1_p21), .A(A2), .B(B2), .C(C2), .D(D2), .E(E2), .F(F2), .G(G2));
  conv_bcd_2_7seg_4bits conv_bcd_2_7seg_4bits_3 (
    .B0(conv_bin_2_bcd_8bits_1_p14), .B1(conv_bin_2_bcd_8bits_1_p15), .B2(conv_bin_2_bcd_8bits_1_p16),
    .B3(conv_bin_2_bcd_8bits_1_p17), .A(A1), .B(B1), .C(C1), .D(D1), .E(E1), .F(F1), .G(G1));
endmodule
