// Digital circuit conv_bin_2_bcd_4bits.dig as structural Verilog
module conv_bin_2_bcd_4bits (
  input  BIN0,
  input  BIN1,
  input  BIN2,
  input  BIN3,
  output S0,
  output S1,
  output S2,
  output S3,
  output S4
);

  LookUpTable #(.Bits(5)) lookuptable_1 (.in0(BIN0), .in1(BIN1), .in2(BIN2), .in3(BIN3), .out({S4, S3, S2, S1, S0}));

  // Notes on the sheet:
  //   contents of lookuptable_1 (hex, n*v repeats v):
  //   0,1,2,3,4,5,6,7,8,9,10,11,12,13,14,15
endmodule
