// Digital circuit 1s-complement_4bits.dig as structural Verilog
module _1s_complement_4bits (
  input  [3:0] X_4b,
  output [3:0] X_4b_2
);

  not not_1 (X_4b_2[0], X_4b[0]);
  not not_2 (X_4b_2[1], X_4b[1]);
  not not_3 (X_4b_2[2], X_4b[2]);
  not not_4 (X_4b_2[3], X_4b[3]);
endmodule
