// Digital circuit increment_4bits.dig as structural Verilog
module increment_4bits (
  input  [3:0] X_4b,
  output [3:0] Y_4b,
  output Carry_out
);

  wire half_adder_1bit_1_cout, half_adder_1bit_2_cout, half_adder_1bit_3_cout;

  half_adder_1bit half_adder_1bit_1 (.A(1'b1), .B(X_4b[0]), .S(Y_4b[0]), .Cout(half_adder_1bit_1_cout));
  half_adder_1bit half_adder_1bit_2 (
    .A(X_4b[1]), .B(half_adder_1bit_1_cout), .S(Y_4b[1]), .Cout(half_adder_1bit_2_cout));
  half_adder_1bit half_adder_1bit_3 (
    .A(X_4b[2]), .B(half_adder_1bit_2_cout), .S(Y_4b[2]), .Cout(half_adder_1bit_3_cout));
  half_adder_1bit half_adder_1bit_4 (.A(X_4b[3]), .B(half_adder_1bit_3_cout), .S(Y_4b[3]), .Cout(Carry_out));
endmodule
