// Digital circuit modal_2s-complement_4bits.dig as structural Verilog
module modal_2s_complement_4bits (
  input  [3:0] X_4b,
  input  Selecteur_2s_complement4bits_1Scomp_et_increment,
  input  Selecteur_Increment_1scomplement4bits,
  output [3:0] Y_4b,
  output Carry_out
);

  wire _2s_complement_4bits_1_cout, increment_4bits_1_carry_out;
  wire [3:0] _1s_complement_4bits_1_x_4b_2, _2s_complement_4bits_1_a3, demultiplexer_1_out_0,
       demultiplexer_1_out_1, demultiplexer_2_out_0, demultiplexer_2_out_1, increment_4bits_1_y_4b, or_1_out;

  Demultiplexer #(.Bits(4)) demultiplexer_1 (
    .sel(Selecteur_2s_complement4bits_1Scomp_et_increment), .in(X_4b), .out_0(demultiplexer_1_out_0),
    .out_1(demultiplexer_1_out_1));
  Demultiplexer #(.Bits(4)) demultiplexer_2 (
    .sel(Selecteur_Increment_1scomplement4bits), .in(demultiplexer_1_out_0), .out_0(demultiplexer_2_out_0),
    .out_1(demultiplexer_2_out_1));
  _2s_complement_4bits _2s_complement_4bits_1 (
    .A0(demultiplexer_1_out_1[0]), .A1_2(demultiplexer_1_out_1[1]), .A2_2(demultiplexer_1_out_1[2]),
    .A3_2(demultiplexer_1_out_1[3]), .A3(_2s_complement_4bits_1_a3[3]), .A2(_2s_complement_4bits_1_a3[2]),
    .A1(_2s_complement_4bits_1_a3[1]), .A0_2(_2s_complement_4bits_1_a3[0]), .cout(_2s_complement_4bits_1_cout));
  _1s_complement_4bits _1s_complement_4bits_1 (.X_4b(demultiplexer_2_out_0), .X_4b_2(_1s_complement_4bits_1_x_4b_2));
  increment_4bits increment_4bits_1 (
    .X_4b(demultiplexer_2_out_1), .Y_4b(increment_4bits_1_y_4b), .Carry_out(increment_4bits_1_carry_out));
  assign or_1_out = _1s_complement_4bits_1_x_4b_2 | increment_4bits_1_y_4b;  // Or or_1, 4 bits wide
  assign Y_4b = or_1_out | _2s_complement_4bits_1_a3;  // Or or_2, 4 bits wide
  or or_3 (Carry_out, increment_4bits_1_carry_out, _2s_complement_4bits_1_cout);
endmodule
