// Digital circuit tp1_2s-complement_8bits.dig as structural Verilog
module tp1_2s_complement_8bits (
  input  [7:0] A,
  output [7:0] C,
  output \Bit_supplémentaire 
);

  wire not_1_out, not_2_out, not_3_out, not_4_out, not_5_out, not_6_out, not_7_out, not_8_out,
       tp1_half_adder_1bit_1_cout, tp1_half_adder_1bit_2_cout, tp1_half_adder_1bit_3_cout,
       tp1_half_adder_1bit_4_cout, tp1_half_adder_1bit_5_cout, tp1_half_adder_1bit_6_cout,
       tp1_half_adder_1bit_7_cout;

  not not_1 (not_1_out, A[7]);
  not not_2 (not_2_out, A[6]);
  not not_3 (not_3_out, A[5]);
  not not_4 (not_4_out, A[4]);
  not not_5 (not_5_out, A[3]);
  not not_6 (not_6_out, A[2]);
  not not_7 (not_7_out, A[1]);
  not not_8 (not_8_out, A[0]);
  tp1_half_adder_1bit tp1_half_adder_1bit_1 (.A(not_8_out), .B(1'b1), .S(C[0]), .Cout(tp1_half_adder_1bit_1_cout));
  tp1_half_adder_1bit tp1_half_adder_1bit_2 (
    .A(not_7_out), .B(tp1_half_adder_1bit_1_cout), .S(C[1]), .Cout(tp1_half_adder_1bit_2_cout));
  tp1_half_adder_1bit tp1_half_adder_1bit_3 (
    .A(not_6_out), .B(tp1_half_adder_1bit_2_cout), .S(C[2]), .Cout(tp1_half_adder_1bit_3_cout));
  tp1_half_adder_1bit tp1_half_adder_1bit_4 (
    .A(not_5_out), .B(tp1_half_adder_1bit_3_cout), .S(C[3]), .Cout(tp1_half_adder_1bit_4_cout));
  tp1_half_adder_1bit tp1_half_adder_1bit_5 (
    .A(not_4_out), .B(tp1_half_adder_1bit_4_cout), .S(C[4]), .Cout(tp1_half_adder_1bit_5_cout));
  tp1_half_adder_1bit tp1_half_adder_1bit_6 (
    .A(not_3_out), .B(tp1_half_adder_1bit_5_cout), .S(C[5]), .Cout(tp1_half_adder_1bit_6_cout));
  tp1_half_adder_1bit tp1_half_adder_1bit_7 (
    .A(not_2_out), .B(tp1_half_adder_1bit_6_cout), .S(C[6]), .Cout(tp1_half_adder_1bit_7_cout));
  tp1_half_adder_1bit tp1_half_adder_1bit_8 (
    .A(not_1_out), .B(tp1_half_adder_1bit_7_cout), .S(C[7]), .Cout(\Bit_supplémentaire ));
endmodule
