// Digital circuit tp1_full-adder_1bit.dig as structural Verilog
module tp1_full_adder_1bit (
  input  A,
  input  B,
  input  Cin,
  output S,
  output Cout
);

  wire and_1_out, and_2_out, or_1_out, tp1_half_adder_1bit_1_cout, tp1_half_adder_1bit_1_s;

  and and_1 (and_1_out, A, Cin);
  tp1_half_adder_1bit tp1_half_adder_1bit_1 (
    .A(A), .B(B), .S(tp1_half_adder_1bit_1_s), .Cout(tp1_half_adder_1bit_1_cout));
  and and_2 (and_2_out, B, Cin);
  xor xor_1 (S, tp1_half_adder_1bit_1_s, Cin);
  or or_1 (or_1_out, tp1_half_adder_1bit_1_cout, and_1_out);
  or or_2 (Cout, or_1_out, and_2_out);
endmodule

/* Test case test-fulladder:
Cin	A	B  	S 	Cout
0 	0	0	0	0
0	0	1	1	0
0	1	0	1	0
0	1	1	0	1
1	0	0	1	0
1	0	1	0	1
1	1	0	0	1
1	1	1	1	1
*/
