// Digital circuit tp1_full-adder_8bits.dig as structural Verilog
module tp1_full_adder_8bits (
  input  [7:0] A,
  input  [7:0] B,
  input  Cin,
  output [7:0] S,
  output Cout
);

  wire tp1_full_adder_1bit_1_cout, tp1_full_adder_1bit_2_cout, tp1_full_adder_1bit_3_cout,
       tp1_full_adder_1bit_4_cout, tp1_full_adder_1bit_5_cout, tp1_full_adder_1bit_6_cout,
       tp1_full_adder_1bit_7_cout;

  tp1_full_adder_1bit tp1_full_adder_1bit_1 (
    .A(A[0]), .B(B[0]), .Cin(Cin), .S(S[0]), .Cout(tp1_full_adder_1bit_1_cout));
  tp1_full_adder_1bit tp1_full_adder_1bit_2 (
    .A(A[1]), .B(B[1]), .Cin(tp1_full_adder_1bit_1_cout), .S(S[1]), .Cout(tp1_full_adder_1bit_2_cout));
  tp1_full_adder_1bit tp1_full_adder_1bit_3 (
    .A(A[2]), .B(B[2]), .Cin(tp1_full_adder_1bit_2_cout), .S(S[2]), .Cout(tp1_full_adder_1bit_3_cout));
  tp1_full_adder_1bit tp1_full_adder_1bit_4 (
    .A(A[3]), .B(B[3]), .Cin(tp1_full_adder_1bit_3_cout), .S(S[3]), .Cout(tp1_full_adder_1bit_4_cout));
  tp1_full_adder_1bit tp1_full_adder_1bit_5 (
    .A(A[4]), .B(B[4]), .Cin(tp1_full_adder_1bit_4_cout), .S(S[4]), .Cout(tp1_full_adder_1bit_5_cout));
  tp1_full_adder_1bit tp1_full_adder_1bit_6 (
    .A(A[5]), .B(B[5]), .Cin(tp1_full_adder_1bit_5_cout), .S(S[5]), .Cout(tp1_full_adder_1bit_6_cout));
  tp1_full_adder_1bit tp1_full_adder_1bit_7 (
    .A(A[6]), .B(B[6]), .Cin(tp1_full_adder_1bit_6_cout), .S(S[6]), .Cout(tp1_full_adder_1bit_7_cout));
  tp1_full_adder_1bit tp1_full_adder_1bit_8 (
    .A(A[7]), .B(B[7]), .Cin(tp1_full_adder_1bit_7_cout), .S(S[7]), .Cout(Cout));
endmodule

/* Test case:
Cin A B Cout S

loop(A,256)
  loop(B,256)
    0 (A) (B) ((A+B)>>8) (A+B)
    1 (A) (B) ((A+B+1)>>8) (A+B+1)
  end loop
end loop
*/
