// Digital circuit tp1_half-adder_1bit.dig as structural Verilog
module tp1_half_adder_1bit (
  input  A,
  input  B,
  output S,
  output Cout
);

  xor xor_1 (S, A, B);
  and and_1 (Cout, A, B);
endmodule
