// Digital circuit tp2_afficheur_bin_2_7seg_4bits.dig as structural Verilog
module tp2_afficheur_bin_2_7seg_4bits (
  input  BIN0,
  input  BIN1,
  input  BIN2,
  input  BIN3,
  input  E
);

  wire tp2_conv_bin_2_7seg_4bits_1_a0, tp2_conv_bin_2_7seg_4bits_1_a1, tp2_conv_bin_2_7seg_4bits_1_b0,
       tp2_conv_bin_2_7seg_4bits_1_b1, tp2_conv_bin_2_7seg_4bits_1_c0, tp2_conv_bin_2_7seg_4bits_1_c1,
       tp2_conv_bin_2_7seg_4bits_1_d0, tp2_conv_bin_2_7seg_4bits_1_d1, tp2_conv_bin_2_7seg_4bits_1_e0,
       tp2_conv_bin_2_7seg_4bits_1_e1, tp2_conv_bin_2_7seg_4bits_1_f0, tp2_conv_bin_2_7seg_4bits_1_f1,
       tp2_conv_bin_2_7seg_4bits_1_g0, tp2_conv_bin_2_7seg_4bits_1_g1;

  Seven_Seg seven_seg_1 (
    .a(tp2_conv_bin_2_7seg_4bits_1_a1), .b(tp2_conv_bin_2_7seg_4bits_1_b1),
    .c(tp2_conv_bin_2_7seg_4bits_1_c1), .d(tp2_conv_bin_2_7seg_4bits_1_d1),
    .e(tp2_conv_bin_2_7seg_4bits_1_e1), .f(tp2_conv_bin_2_7seg_4bits_1_f1),
    .g(tp2_conv_bin_2_7seg_4bits_1_g1), .dp(1'b0));
  tp2_conv_bin_2_7seg_4bits tp2_conv_bin_2_7seg_4bits_1 (
    .BIN0(BIN0), .BIN1(BIN1), .BIN2(BIN2), .BIN3(BIN3), .E(E), .A0(tp2_conv_bin_2_7seg_4bits_1_a0),
    .B0(tp2_conv_bin_2_7seg_4bits_1_b0), .C0(tp2_conv_bin_2_7seg_4bits_1_c0),
    .D0(tp2_conv_bin_2_7seg_4bits_1_d0), .E0(tp2_conv_bin_2_7seg_4bits_1_e0),
    .F0(tp2_conv_bin_2_7seg_4bits_1_f0), .G0(tp2_conv_bin_2_7seg_4bits_1_g0),
    .A1(tp2_conv_bin_2_7seg_4bits_1_a1), .B1(tp2_conv_bin_2_7seg_4bits_1_b1),
    .C1(tp2_conv_bin_2_7seg_4bits_1_c1), .D1(tp2_conv_bin_2_7seg_4bits_1_d1),
    .E1(tp2_conv_bin_2_7seg_4bits_1_e1), .F1(tp2_conv_bin_2_7seg_4bits_1_f1),
    .G1(tp2_conv_bin_2_7seg_4bits_1_g1));
  Seven_Seg seven_seg_2 (
    .a(tp2_conv_bin_2_7seg_4bits_1_a0), .b(tp2_conv_bin_2_7seg_4bits_1_b0),
    .c(tp2_conv_bin_2_7seg_4bits_1_c0), .d(tp2_conv_bin_2_7seg_4bits_1_d0),
    .e(tp2_conv_bin_2_7seg_4bits_1_e0), .f(tp2_conv_bin_2_7seg_4bits_1_f0),
    .g(tp2_conv_bin_2_7seg_4bits_1_g0), .dp(1'b0));
endmodule
