// Digital circuit tp2_afficheur_bin_2_7seg_8bits.dig as structural Verilog
module tp2_afficheur_bin_2_7seg_8bits (
  input  [7:0] I
);

  wire [6:0] tp2_conv_bin_2_7seg_8bits_1_c_7seg, tp2_conv_bin_2_7seg_8bits_1_d_7seg,
       tp2_conv_bin_2_7seg_8bits_1_s_7seg, tp2_conv_bin_2_7seg_8bits_1_u_7seg;

  tp2_conv_bin_2_7seg_8bits tp2_conv_bin_2_7seg_8bits_1 (
    .I(I), .U_7seg(tp2_conv_bin_2_7seg_8bits_1_u_7seg), .D_7seg(tp2_conv_bin_2_7seg_8bits_1_d_7seg),
    .C_7seg(tp2_conv_bin_2_7seg_8bits_1_c_7seg), .S_7seg(tp2_conv_bin_2_7seg_8bits_1_s_7seg));
  Seven_Seg seven_seg_1 (
    .a(tp2_conv_bin_2_7seg_8bits_1_s_7seg[0]), .b(tp2_conv_bin_2_7seg_8bits_1_s_7seg[1]),
    .c(tp2_conv_bin_2_7seg_8bits_1_s_7seg[2]), .d(tp2_conv_bin_2_7seg_8bits_1_s_7seg[3]),
    .e(tp2_conv_bin_2_7seg_8bits_1_s_7seg[4]), .f(tp2_conv_bin_2_7seg_8bits_1_s_7seg[5]),
    .g(tp2_conv_bin_2_7seg_8bits_1_s_7seg[6]), .dp(1'b0));
  Seven_Seg seven_seg_2 (
    .a(tp2_conv_bin_2_7seg_8bits_1_c_7seg[0]), .b(tp2_conv_bin_2_7seg_8bits_1_c_7seg[1]),
    .c(tp2_conv_bin_2_7seg_8bits_1_c_7seg[2]), .d(tp2_conv_bin_2_7seg_8bits_1_c_7seg[3]),
    .e(tp2_conv_bin_2_7seg_8bits_1_c_7seg[4]), .f(tp2_conv_bin_2_7seg_8bits_1_c_7seg[5]),
    .g(tp2_conv_bin_2_7seg_8bits_1_c_7seg[6]), .dp(1'b0));
  Seven_Seg seven_seg_3 (
    .a(tp2_conv_bin_2_7seg_8bits_1_d_7seg[0]), .b(tp2_conv_bin_2_7seg_8bits_1_d_7seg[1]),
    .c(tp2_conv_bin_2_7seg_8bits_1_d_7seg[2]), .d(tp2_conv_bin_2_7seg_8bits_1_d_7seg[3]),
    .e(tp2_conv_bin_2_7seg_8bits_1_d_7seg[4]), .f(tp2_conv_bin_2_7seg_8bits_1_d_7seg[5]),
    .g(tp2_conv_bin_2_7seg_8bits_1_d_7seg[6]), .dp(1'b0));
  Seven_Seg seven_seg_4 (
    .a(tp2_conv_bin_2_7seg_8bits_1_u_7seg[0]), .b(tp2_conv_bin_2_7seg_8bits_1_u_7seg[1]),
    .c(tp2_conv_bin_2_7seg_8bits_1_u_7seg[2]), .d(tp2_conv_bin_2_7seg_8bits_1_u_7seg[3]),
    .e(tp2_conv_bin_2_7seg_8bits_1_u_7seg[4]), .f(tp2_conv_bin_2_7seg_8bits_1_u_7seg[5]),
    .g(tp2_conv_bin_2_7seg_8bits_1_u_7seg[6]), .dp(1'b0));

  // Notes on the sheet:
  //   I: Entrée sur 8 bits en complément à 2.
  //   Afficheur 7 segments capable de représenter 
  //   en signe magnitude 
  //   un nombre en complément à 2 sur 8 bits
  //   Afficheur 7 segments
endmodule
