// Digital circuit tp2_conv_bcd_2_7seg_4bits.dig as structural Verilog
module tp2_conv_bcd_2_7seg_4bits (
  input  [3:0] I,
  output [6:0] S
);

  LookUpTable #(.Bits(7)) lookuptable_1 (.in0(I[0]), .in1(I[1]), .in2(I[2]), .in3(I[3]), .out(S));

  // Notes on the sheet:
  //   I: Entrée en codage BCD sur 4 bits
  //   contents of lookuptable_1 (hex, n*v repeats v):
  //   3f,6,5b,4f,66,6d,7d,7,7f,6f,4*0,40,79
endmodule
