// Digital circuit tp2_conv_bin_2_7seg_4bits.dig as structural Verilog
module tp2_conv_bin_2_7seg_4bits (
  input  BIN0,
  input  BIN1,
  input  BIN2,
  input  BIN3,
  input  E,
  output A0,
  output B0,
  output C0,
  output D0,
  output E0,
  output F0,
  output G0,
  output A1,
  output B1,
  output C1,
  output D1,
  output E1,
  output F1,
  output G1
);

  wire tp2_conv_bin_2_bcd_4bits_1_s0, tp2_conv_bin_2_bcd_4bits_1_s1, tp2_conv_bin_2_bcd_4bits_1_s2,
       tp2_conv_bin_2_bcd_4bits_1_s3, tp2_conv_bin_2_bcd_4bits_1_s4, tp2_conv_bin_2_bcd_4bits_1_s5,
       tp2_conv_bin_2_bcd_4bits_1_s6, tp2_conv_bin_2_bcd_4bits_1_s7;
  wire [3:0] or_1_out, or_5_out;

  tp2_conv_bin_2_bcd_4bits tp2_conv_bin_2_bcd_4bits_1 (
    .BIN0(BIN0), .BIN1(BIN1), .BIN2(BIN2), .BIN3(BIN3), .S0(tp2_conv_bin_2_bcd_4bits_1_s0),
    .S1(tp2_conv_bin_2_bcd_4bits_1_s1), .S2(tp2_conv_bin_2_bcd_4bits_1_s2),
    .S3(tp2_conv_bin_2_bcd_4bits_1_s3), .S4(tp2_conv_bin_2_bcd_4bits_1_s4),
    .S5(tp2_conv_bin_2_bcd_4bits_1_s5), .S6(tp2_conv_bin_2_bcd_4bits_1_s6), .S7(tp2_conv_bin_2_bcd_4bits_1_s7));
  or or_1 (or_1_out[0], tp2_conv_bin_2_bcd_4bits_1_s0, E);
  or or_2 (or_1_out[1], tp2_conv_bin_2_bcd_4bits_1_s1, E);
  or or_3 (or_1_out[2], tp2_conv_bin_2_bcd_4bits_1_s2, E);
  or or_4 (or_1_out[3], tp2_conv_bin_2_bcd_4bits_1_s3, E);
  or or_5 (or_5_out[0], tp2_conv_bin_2_bcd_4bits_1_s4, E);
  or or_6 (or_5_out[1], tp2_conv_bin_2_bcd_4bits_1_s5, E);
  or or_7 (or_5_out[2], tp2_conv_bin_2_bcd_4bits_1_s6, E);
  or or_8 (or_5_out[3], tp2_conv_bin_2_bcd_4bits_1_s7, E);
  tp2_conv_bcd_2_7seg_4bits tp2_conv_bcd_2_7seg_4bits_1 (.I(or_1_out), .S({G0, F0, E0, D0, C0, B0, A0}));
  tp2_conv_bcd_2_7seg_4bits tp2_conv_bcd_2_7seg_4bits_2 (.I(or_5_out), .S({G1, F1, E1, D1, C1, B1, A1}));
endmodule
