// Digital circuit tp2_conv_bin_2_7seg_8bits.dig as structural Verilog
module tp2_conv_bin_2_7seg_8bits (
  input  [7:0] I,
  output [6:0] U_7seg,
  output [6:0] D_7seg,
  output [6:0] C_7seg,
  output [6:0] S_7seg
);

  wire [3:0] tp2_conv_bin_2_bcd_8bits_1_c, tp2_conv_bin_2_bcd_8bits_1_d, tp2_conv_bin_2_bcd_8bits_1_s,
       tp2_conv_bin_2_bcd_8bits_1_u;

  tp2_conv_bin_2_bcd_8bits tp2_conv_bin_2_bcd_8bits_1 (
    .I(I), .U(tp2_conv_bin_2_bcd_8bits_1_u), .D(tp2_conv_bin_2_bcd_8bits_1_d),
    .C(tp2_conv_bin_2_bcd_8bits_1_c), .S(tp2_conv_bin_2_bcd_8bits_1_s));
  tp2_conv_bcd_2_7seg_4bits tp2_conv_bcd_2_7seg_4bits_1 (.I(tp2_conv_bin_2_bcd_8bits_1_u), .S(U_7seg));
  tp2_conv_bcd_2_7seg_4bits tp2_conv_bcd_2_7seg_4bits_2 (.I(tp2_conv_bin_2_bcd_8bits_1_d), .S(D_7seg));
  tp2_conv_bcd_2_7seg_4bits tp2_conv_bcd_2_7seg_4bits_3 (.I(tp2_conv_bin_2_bcd_8bits_1_c), .S(C_7seg));
  tp2_conv_bcd_2_7seg_4bits tp2_conv_bcd_2_7seg_4bits_4 (.I(tp2_conv_bin_2_bcd_8bits_1_s), .S(S_7seg));

  // Notes on the sheet:
  //   I: Entrrée sur 8 bits en complément à 2.
  //   U_7seg: Codage 7 segment des unités
  //   D_7seg: Codage 7 segment des dizaines
  //   C_7seg: Codage 7 segment des centaines
  //   S_7seg: Codage 7 segment du signe
endmodule
