// Digital circuit tp2_conv_bin_2_bcd_8bits.dig as structural Verilog
module tp2_conv_bin_2_bcd_8bits (
  input  [7:0] I,
  output [3:0] U,
  output [3:0] D,
  output [3:0] C,
  output [3:0] S
);

  wire [3:3] tp2_conv_bin_2_sbin_8bits_1_e;
  wire [6:0] tp2_conv_bin_2_sbin_8bits_1_m;
  wire [11:0] rom_1_d;

  tp2_conv_bin_2_sbin_8bits tp2_conv_bin_2_sbin_8bits_1 (
    .I(I), .M(tp2_conv_bin_2_sbin_8bits_1_m), .S(S[3]), .E(tp2_conv_bin_2_sbin_8bits_1_e[3]));
  ROM #(.AddrBits(7), .Bits(12)) rom_1 (.A(tp2_conv_bin_2_sbin_8bits_1_m), .sel(1'b1), .D(rom_1_d));
  assign U = rom_1_d[3:0] | {4{tp2_conv_bin_2_sbin_8bits_1_e[3]}};  // Or or_1, 4 bits wide
  assign D = rom_1_d[7:4] | {4{tp2_conv_bin_2_sbin_8bits_1_e[3]}};  // Or or_2, 4 bits wide
  assign C = rom_1_d[11:8] | {4{tp2_conv_bin_2_sbin_8bits_1_e[3]}};  // Or or_3, 4 bits wide

  assign S[2:0] = {{2{S[3]}}, 1'b0};

  // Notes on the sheet:
  //   I: Entrrée sur 8 bits en complément à 2.
  //   U: Chiffre des unités en BCD, 
  //   ou code BCD pour 'E' (1111) si nécessaire
  //   D: Chiffre des dizaines en BCD,
  //   ou code BCD pour 'E' (1111) si nécessaire
  //   C: Chiffre des centaines en BCD,
  //   ou code BCD pour 'E' (1111) si nécessaire
  //   S: Signe en BCD (1110)
  //   contents of rom_1 (hex, n*v repeats v):
  //   0,1,2,3,4,5,6,7,8,9,10,11,12,13,14,15,16,17,18,19,20,21,22,23
  //   ,24,25,26,27,28,29,30,31,32,33,34,35,36,37,38,39,40,41,42,43,44
  //   ,45,46,47,48,49,50,51,52,53,54,55,56,57,58,59,60,61,62,63,64,65
  //   ,66,67,68,69,70,71,72,73,74,75,76,77,78,79,80,81,82,83,84,85,86
  //   ,87,88,89,90,91,92,93,94,95,96,97,98,99,100,101,102,103,104,105
  //   ,106,107,108,109,110,111,112,113,114,115,116,117,118,119,120,121
  //   ,122,123,124,125,126,127
endmodule
