// Digital circuit tp2_conv_bin_2_sbin_8bits.dig as structural Verilog
module tp2_conv_bin_2_sbin_8bits (
  input  [7:0] I,
  output [6:0] M,
  output S,
  output E
);

  wire tp1_half_adder_1bit_1_cout, tp1_half_adder_1bit_2_cout, tp1_half_adder_1bit_3_cout,
       tp1_half_adder_1bit_4_cout, tp1_half_adder_1bit_5_cout, tp1_half_adder_1bit_6_cout, xor_1_out,
       xor_2_out, xor_3_out, xor_4_out, xor_5_out, xor_6_out, xor_7_out;

  xor xor_1 (xor_1_out, I[6], I[7]);
  xor xor_2 (xor_2_out, I[5], I[7]);
  xor xor_3 (xor_3_out, I[4], I[7]);
  xor xor_4 (xor_4_out, I[3], I[7]);
  xor xor_5 (xor_5_out, I[2], I[7]);
  xor xor_6 (xor_6_out, I[1], I[7]);
  xor xor_7 (xor_7_out, I[0], I[7]);
  tp1_half_adder_1bit tp1_half_adder_1bit_1 (.A(xor_7_out), .B(I[7]), .S(M[0]), .Cout(tp1_half_adder_1bit_1_cout));
  tp1_half_adder_1bit tp1_half_adder_1bit_2 (
    .A(xor_6_out), .B(tp1_half_adder_1bit_1_cout), .S(M[1]), .Cout(tp1_half_adder_1bit_2_cout));
  tp1_half_adder_1bit tp1_half_adder_1bit_3 (
    .A(xor_5_out), .B(tp1_half_adder_1bit_2_cout), .S(M[2]), .Cout(tp1_half_adder_1bit_3_cout));
  tp1_half_adder_1bit tp1_half_adder_1bit_4 (
    .A(xor_4_out), .B(tp1_half_adder_1bit_3_cout), .S(M[3]), .Cout(tp1_half_adder_1bit_4_cout));
  tp1_half_adder_1bit tp1_half_adder_1bit_5 (
    .A(xor_3_out), .B(tp1_half_adder_1bit_4_cout), .S(M[4]), .Cout(tp1_half_adder_1bit_5_cout));
  tp1_half_adder_1bit tp1_half_adder_1bit_6 (
    .A(xor_2_out), .B(tp1_half_adder_1bit_5_cout), .S(M[5]), .Cout(tp1_half_adder_1bit_6_cout));
  tp1_half_adder_1bit tp1_half_adder_1bit_7 (.A(xor_1_out), .B(tp1_half_adder_1bit_6_cout), .S(M[6]), .Cout(E));

  assign S = I[7];

  // Notes on the sheet:
  //   I: Input sur 8 bit en complément à 2
  //   M: Output sur 7 bits positive (magnitude)
  //   S: Signe
  //   E: Erreur: en cas d'overflow
endmodule
