// Digital circuit tp3_afficheur_calculatrice.dig as structural Verilog
module tp3_afficheur_calculatrice (
  input  [7:0] A,
  input  [7:0] B,
  input  Addition,
  input  Soustraction,
  input  Affichage_A,
  input  Affichage_B
);

  wire [6:0] tp3_calculateur_8bits_1_c_7seg, tp3_calculateur_8bits_1_d_7seg, tp3_calculateur_8bits_1_s_7seg,
       tp3_calculateur_8bits_1_u_7seg;

  tp3_calculateur_8bits tp3_calculateur_8bits_1 (
    .A(A), .B(B), .Addition(Addition), .Soustraction(Soustraction), .Affichage_A(Affichage_A),
    .Affichage_B(Affichage_B), .U_7seg(tp3_calculateur_8bits_1_u_7seg),
    .D_7seg(tp3_calculateur_8bits_1_d_7seg), .C_7seg(tp3_calculateur_8bits_1_c_7seg),
    .S_7seg(tp3_calculateur_8bits_1_s_7seg));
  Seven_Seg seven_seg_1 (
    .a(tp3_calculateur_8bits_1_s_7seg[0]), .b(tp3_calculateur_8bits_1_s_7seg[1]),
    .c(tp3_calculateur_8bits_1_s_7seg[2]), .d(tp3_calculateur_8bits_1_s_7seg[3]),
    .e(tp3_calculateur_8bits_1_s_7seg[4]), .f(tp3_calculateur_8bits_1_s_7seg[5]),
    .g(tp3_calculateur_8bits_1_s_7seg[6]), .dp(1'b0));
  Seven_Seg seven_seg_2 (
    .a(tp3_calculateur_8bits_1_c_7seg[0]), .b(tp3_calculateur_8bits_1_c_7seg[1]),
    .c(tp3_calculateur_8bits_1_c_7seg[2]), .d(tp3_calculateur_8bits_1_c_7seg[3]),
    .e(tp3_calculateur_8bits_1_c_7seg[4]), .f(tp3_calculateur_8bits_1_c_7seg[5]),
    .g(tp3_calculateur_8bits_1_c_7seg[6]), .dp(1'b0));
  Seven_Seg seven_seg_3 (
    .a(tp3_calculateur_8bits_1_d_7seg[0]), .b(tp3_calculateur_8bits_1_d_7seg[1]),
    .c(tp3_calculateur_8bits_1_d_7seg[2]), .d(tp3_calculateur_8bits_1_d_7seg[3]),
    .e(tp3_calculateur_8bits_1_d_7seg[4]), .f(tp3_calculateur_8bits_1_d_7seg[5]),
    .g(tp3_calculateur_8bits_1_d_7seg[6]), .dp(1'b0));
  Seven_Seg seven_seg_4 (
    .a(tp3_calculateur_8bits_1_u_7seg[0]), .b(tp3_calculateur_8bits_1_u_7seg[1]),
    .c(tp3_calculateur_8bits_1_u_7seg[2]), .d(tp3_calculateur_8bits_1_u_7seg[3]),
    .e(tp3_calculateur_8bits_1_u_7seg[4]), .f(tp3_calculateur_8bits_1_u_7seg[5]),
    .g(tp3_calculateur_8bits_1_u_7seg[6]), .dp(1'b0));

  // Notes on the sheet:
  //   A: Entrée en complément à 2 sur 8 bits
  //   B: Entrée en complément à 2 sur 8 bits
  //   Addition: Calcul A + B
  //   Soustraction: Calcul A - B
  //   Affichage_A: Affiche A en sortie
  //   Affichage_B: Affiche B en sortie
  //   Afficheur 7 segments
  //   Afficheur 7 segments capable de représenter 
  //   en signe magnitude 
  //   un nombre en complément à 2 sur 8 bits
endmodule
