// Digital circuit tp3_calculateur-8bits-wraper-BASYS3.dig as structural Verilog
module tp3_calculateur_8bits_wraper_BASYS3 (
  input  Clock,
  input  SW0,
  input  SW1,
  input  SW2,
  input  SW3,
  input  SW4,
  input  SW5,
  input  SW6,
  input  SW7,
  input  SW8,
  input  SW9,
  input  SW10,
  input  SW11,
  input  SW12,
  input  SW13,
  input  SW14,
  input  SW15,
  input  Up,
  input  Down,
  input  Right,
  input  Left,
  output AN3,
  output AN2,
  output AN1,
  output AN0,
  output CD,
  output CC,
  output CB,
  output CA,
  output CE,
  output CF,
  output CG,
  output LED0,
  output LED1,
  output LED2,
  output LED3,
  output LED4,
  output LED5,
  output LED6,
  output LED7,
  output LED8,
  output LED9,
  output LED10,
  output LED11,
  output LED12,
  output LED13,
  output LED14,
  output LED15
);

  wire decoder_1_out_0, decoder_1_out_1, decoder_1_out_2, decoder_1_out_3;
  wire [1:0] counter_1_out;
  wire [6:0] calc_8bits_c_7seg, calc_8bits_d_7seg, calc_8bits_s_7seg, calc_8bits_u_7seg, multiplexer_1_out;

  tp3_calculateur_8bits calc_8bits (
    .A({SW7, SW6, SW5, SW4, SW3, SW2, SW1, SW0}), .B({SW15, SW14, SW13, SW12, SW11, SW10, SW9, SW8}),
    .Addition(Up), .Soustraction(Down), .Affichage_A(Right), .Affichage_B(Left), .U_7seg(calc_8bits_u_7seg),
    .D_7seg(calc_8bits_d_7seg), .C_7seg(calc_8bits_c_7seg), .S_7seg(calc_8bits_s_7seg));
  Counter #(.Bits(2)) counter_1 (.en(1'b1), .C(Clock), .clr(1'b0), .out(counter_1_out));  // open: ovf
  not not_1 (CG, multiplexer_1_out[6]);
  not not_2 (CF, multiplexer_1_out[5]);
  not not_3 (CE, multiplexer_1_out[4]);
  not not_4 (CD, multiplexer_1_out[3]);
  not not_5 (CC, multiplexer_1_out[2]);
  not not_6 (CB, multiplexer_1_out[1]);
  not not_7 (CA, multiplexer_1_out[0]);
  Decoder #(.Selector_Bits(2)) decoder_1 (
    .sel(counter_1_out), .out_0(decoder_1_out_0), .out_1(decoder_1_out_1), .out_2(decoder_1_out_2),
    .out_3(decoder_1_out_3));
  Multiplexer #(.Selector_Bits(2), .Bits(7)) multiplexer_1 (
    .sel(counter_1_out), .in_0(calc_8bits_u_7seg), .in_1(calc_8bits_d_7seg), .in_2(calc_8bits_c_7seg),
    .in_3(calc_8bits_s_7seg), .out(multiplexer_1_out));
  not not_8 (AN0, decoder_1_out_0);
  not not_9 (AN1, decoder_1_out_1);
  not not_10 (AN2, decoder_1_out_2);
  not not_11 (AN3, decoder_1_out_3);

  assign LED0 = SW0;
  assign LED1 = SW1;
  assign LED2 = SW2;
  assign LED3 = SW3;
  assign LED4 = SW4;
  assign LED5 = SW5;
  assign LED6 = SW6;
  assign LED7 = SW7;
  assign LED8 = SW8;
  assign LED9 = SW9;
  assign LED10 = SW10;
  assign LED11 = SW11;
  assign LED12 = SW12;
  assign LED13 = SW13;
  assign LED14 = SW14;
  assign LED15 = SW15;

  // Notes on the sheet:
  //   Clock: pin W5, Hz: 200
  //   SW0: pin V17
  //   SW1: pin V16
  //   SW2: pin W16
  //   SW3: pin W17
  //   SW4: pin W15
  //   SW5: pin V15
  //   SW6: pin W14
  //   SW7: pin W13
  //   SW8: pin V2
  //   SW9: pin T3
  //   SW10: pin T2
  //   SW11: pin R3
  //   SW12: pin W2
  //   SW13: pin U1
  //   SW14: pin T1
  //   SW15: pin R2
  //   AN3: pin W4
  //   AN2: pin V4
  //   AN1: pin U4
  //   AN0: pin U2
  //   CD: pin V8
  //   CC: pin U8
  //   CB: pin W6
  //   CA: pin W7
  //   CE: pin U5
  //   CF: pin V5
  //   CG: pin U7
  //   Up: pin T18
  //   LED0: pin U16
  //   LED1: pin E19
  //   LED2: pin U19
  //   LED3: pin V19
  //   LED4: pin W18
  //   LED5: pin U15
  //   LED6: pin U14
  //   LED7: pin V14
  //   LED8: pin V13
  //   LED9: pin V3
  //   LED10: pin W3
  //   LED11: pin U3
  //   LED12: pin P3
  //   LED13: pin N3
  //   LED14: pin P1
  //   LED15: pin L1
  //   Down: pin U17
  //   Right: pin T17
  //   Left: pin W19
  //   Digital Cross
  //   LED's
  //   Switches
  //   Seven Segment Display
endmodule
