// Digital circuit tp3_calculateur_8bits.dig as structural Verilog
module tp3_calculateur_8bits (
  input  [7:0] A,
  input  [7:0] B,
  input  Addition,
  input  Soustraction,
  input  Affichage_A,
  input  Affichage_B,
  output [6:0] U_7seg,
  output [6:0] D_7seg,
  output [6:0] C_7seg,
  output [6:0] S_7seg
);

  wire or_1_out;
  wire [1:0] priorityencoder_1_num;
  wire [7:0] and_1_out, bitextender_1_out, multiplexer_1_out, tp1_2s_complement_8bits_1_c,
       tp1_full_adder_8bits_1_s, tp1_full_adder_8bits_2_s;

  tp1_2s_complement_8bits tp1_2s_complement_8bits_1 (
    .A(B), .C(tp1_2s_complement_8bits_1_c));  // open: Bit_supplémentaire
  PriorityEncoder #(.Selector_Bits(2)) priorityencoder_1 (
    .in0(Affichage_A), .in1(Affichage_B), .in2(Addition), .in3(Soustraction), .num(priorityencoder_1_num));  // open: any
  or or_1 (or_1_out, Soustraction, Addition, Affichage_B, Affichage_A);
  tp1_full_adder_8bits tp1_full_adder_8bits_1 (.A(A), .B(B), .Cin(1'b0), .S(tp1_full_adder_8bits_1_s));  // open: Cout
  tp1_full_adder_8bits tp1_full_adder_8bits_2 (
    .A(A), .B(tp1_2s_complement_8bits_1_c), .Cin(1'b0), .S(tp1_full_adder_8bits_2_s));  // open: Cout
  BitExtender #(.inputBits(1), .outputBits(8)) bitextender_1 (.in(or_1_out), .out(bitextender_1_out));
  // Probe on tp1_full_adder_8bits_2_s
  Multiplexer #(.Selector_Bits(2), .Bits(8)) multiplexer_1 (
    .sel(priorityencoder_1_num), .in_0(A), .in_1(B), .in_2(tp1_full_adder_8bits_1_s),
    .in_3(tp1_full_adder_8bits_2_s), .out(multiplexer_1_out));
  assign and_1_out = multiplexer_1_out & bitextender_1_out;  // And and_1, 8 bits wide
  // Probe on priorityencoder_1_num
  tp2_conv_bin_2_7seg_8bits tp2_conv_bin_2_7seg_8bits_1 (
    .I(and_1_out), .U_7seg(U_7seg), .D_7seg(D_7seg), .C_7seg(C_7seg), .S_7seg(S_7seg));

  // Notes on the sheet:
  //   A: Entrée en complément à 2 sur 8 bits
  //   B: Entrée en complément à 2 sur 8 bits
  //   Addition: Calcul A + B
  //   Soustraction: Calcul A - B
  //   U_7seg: Codage 7 segment des unités
  //   D_7seg: Codage 7 segment des dizaines
  //   C_7seg: Codage 7 segment des centaines
  //   S_7seg: Codage 7 segment du signe
  //   Affichage_A: Affiche A en sortie
  //   Affichage_B: Affiche B en sortie
endmodule
