// Digital circuit serpent_avec_control.dig as structural Verilog
module serpent_avec_control (
  input  D,
  input  U,
  input  C,
  output A00,
  output A01,
  output A02,
  output A03,
  output A04,
  output A05,
  output A10,
  output A11,
  output A12,
  output A13,
  output A14,
  output A15,
  output A20,
  output A21,
  output A22,
  output A23,
  output A24,
  output A25,
  output A30,
  output A31,
  output A32,
  output A33,
  output A34,
  output A35
);

  wire and_1_out, and_2_out, and_3_out, and_4_out, and_5_out, and_6_out, and_7_out, and_8_out, and_9_out,
       and_10_out, and_11_out, and_12_out, and_13_out, and_14_out, and_15_out, and_16_out, and_17_out,
       and_18_out, and_19_out, and_20_out, and_21_out, and_22_out, and_23_out, and_24_out, and_25_out,
       and_26_out, and_27_out, and_28_out, and_29_out, and_30_out, and_31_out, and_32_out, and_33_out,
       and_34_out, and_35_out, and_36_out, and_37_out, and_38_out, not_1_out, not_2_out, not_3_out,
       not_4_out, not_5_out, not_6_out, not_7_out, not_8_out, or_1_out, or_2_out, or_3_out, or_4_out,
       or_5_out, or_6_out, Z_0_n, Z_1_n, Z_2_n, Z_3_n, Z_4_n, Z_5_n;

  not not_1 (not_1_out, D);
  not not_2 (not_2_out, U);
  not not_3 (not_3_out, Z_5_n);
  not not_4 (not_4_out, Z_4_n);
  not not_5 (not_5_out, Z_3_n);
  not not_6 (not_6_out, Z_2_n);
  not not_7 (not_7_out, Z_1_n);
  not not_8 (not_8_out, Z_0_n);
  and and_1 (and_1_out, not_1_out, Z_0_n, Z_1_n, Z_4_n);
  and and_2 (and_2_out, Z_0_n, Z_1_n, Z_3_n, Z_4_n);
  and and_3 (and_3_out, not_8_out, Z_5_n);
  and and_4 (and_4_out, not_7_out, Z_5_n);
  and and_5 (and_5_out, not_1_out, Z_0_n, not_7_out, Z_3_n);
  and and_6 (and_6_out, D, Z_0_n, not_5_out, Z_4_n);
  and and_7 (and_7_out, U, not_8_out, Z_4_n);
  and and_8 (and_8_out, Z_0_n, not_7_out, Z_4_n);
  and and_9 (and_9_out, not_8_out, Z_1_n, Z_4_n);
  and and_10 (and_10_out, Z_0_n, Z_1_n, Z_5_n);
  and and_11 (and_11_out, not_8_out, Z_3_n, Z_4_n);
  and and_12 (and_12_out, D, Z_0_n, Z_1_n, Z_2_n, not_5_out);
  and and_13 (and_13_out, not_1_out, Z_0_n, Z_1_n, not_4_out);
  and and_14 (and_14_out, D, Z_0_n, Z_3_n, not_4_out);
  and and_15 (and_15_out, not_2_out, not_8_out, not_7_out, Z_4_n);
  and and_16 (and_16_out, U, not_8_out, Z_3_n);
  and and_17 (and_17_out, not_8_out, Z_2_n, Z_3_n, not_4_out);
  and and_18 (and_18_out, Z_0_n, Z_1_n, Z_5_n);
  and and_19 (and_19_out, U, not_7_out, Z_2_n, Z_4_n);
  and and_20 (and_20_out, Z_0_n, Z_1_n, not_6_out);
  and and_21 (and_21_out, not_8_out, Z_1_n, Z_2_n);
  and and_22 (and_22_out, Z_0_n, not_7_out, Z_3_n);
  and and_23 (and_23_out, Z_0_n, not_7_out, Z_4_n);
  and and_24 (and_24_out, not_8_out, Z_2_n, not_4_out);
  and and_25 (and_25_out, not_2_out, not_8_out, not_5_out, Z_4_n);
  and and_26 (and_26_out, U, not_8_out, Z_1_n);
  and and_27 (and_27_out, Z_0_n, not_7_out, not_6_out, not_5_out);
  and and_28 (and_28_out, Z_0_n, not_7_out, Z_2_n, Z_4_n);
  and and_29 (and_29_out, Z_0_n, Z_2_n, Z_3_n, not_4_out);
  and and_30 (and_30_out, not_8_out, Z_1_n, not_5_out);
  and and_31 (and_31_out, Z_0_n, Z_5_n);
  and and_32 (and_32_out, Z_1_n, Z_2_n, not_4_out);
  and and_33 (and_33_out, not_1_out, not_7_out, Z_2_n, Z_3_n);
  and and_34 (and_34_out, not_1_out, Z_1_n, not_5_out, not_3_out);
  and and_35 (and_35_out, U, not_8_out);
  and and_36 (and_36_out, not_8_out, not_7_out, not_6_out);
  and and_37 (and_37_out, not_8_out, Z_1_n, not_5_out);
  and and_38 (and_38_out, not_8_out, Z_2_n, not_4_out);
  and and_39 (A00, not_8_out, not_7_out, not_6_out, not_5_out, not_3_out);
  and and_40 (A01, Z_0_n, not_7_out, not_6_out, not_5_out, not_3_out);
  and and_41 (A02, not_8_out, Z_1_n, not_6_out, not_5_out, not_3_out);
  and and_42 (A03, Z_0_n, Z_1_n, not_6_out, not_5_out, not_3_out);
  and and_43 (A04, not_8_out, Z_2_n, not_5_out, not_4_out);
  and and_44 (A05, Z_0_n, Z_2_n, not_5_out, not_4_out);
  and and_45 (A10, not_8_out, Z_1_n, not_6_out, Z_3_n);
  and and_46 (A11, Z_0_n, Z_1_n, not_6_out, Z_3_n);
  and and_47 (A12, not_8_out, not_7_out, Z_2_n, Z_3_n);
  and and_48 (A13, Z_0_n, not_7_out, Z_2_n, Z_3_n);
  and and_49 (A14, not_8_out, Z_1_n, Z_2_n, not_4_out);
  and and_50 (A15, Z_0_n, Z_1_n, Z_2_n, not_4_out);
  and and_51 (A20, not_8_out, not_7_out, Z_2_n, Z_4_n);
  and and_52 (A21, Z_0_n, not_7_out, Z_2_n, Z_4_n);
  and and_53 (A22, not_8_out, Z_1_n, Z_2_n, not_5_out);
  and and_54 (A23, Z_0_n, Z_1_n, Z_2_n, not_5_out);
  and and_55 (A24, not_8_out, not_7_out, not_6_out, Z_3_n);
  and and_56 (A25, Z_0_n, not_7_out, not_6_out, Z_3_n);
  and and_57 (A30, not_8_out, Z_1_n, Z_3_n, Z_4_n);
  and and_58 (A31, Z_0_n, Z_1_n, Z_3_n, Z_4_n);
  and and_59 (A32, not_8_out, not_7_out, Z_5_n);
  and and_60 (A33, Z_0_n, not_7_out, Z_5_n);
  and and_61 (A34, not_8_out, Z_1_n, Z_5_n);
  and and_62 (A35, Z_0_n, Z_1_n, Z_5_n);
  or or_1 (or_1_out, and_1_out, and_2_out, and_3_out, and_4_out);
  or or_2 (or_2_out, and_5_out, and_6_out, and_7_out, and_8_out, and_9_out, and_10_out, and_11_out);
  or or_3 (or_3_out, and_12_out, and_13_out, and_14_out, and_15_out, and_16_out, and_17_out, and_18_out);
  or or_4 (or_4_out, and_19_out, and_20_out, and_21_out, and_22_out, and_23_out, and_24_out);
  or or_5 (or_5_out, and_25_out, and_26_out, and_27_out, and_28_out, and_29_out, and_30_out, and_31_out, and_32_out);
  or or_6 (or_6_out, and_33_out, and_34_out, and_35_out, and_36_out, and_37_out, and_38_out);
  D_FF u_Z_5_n (.D(or_1_out), .C(C), .Q(Z_5_n));  // open: nQ
  D_FF #(.Default(1)) u_Z_4_n (.D(or_2_out), .C(C), .Q(Z_4_n));  // open: nQ
  D_FF #(.Default(1)) u_Z_3_n (.D(or_3_out), .C(C), .Q(Z_3_n));  // open: nQ
  D_FF #(.Default(1)) u_Z_2_n (.D(or_4_out), .C(C), .Q(Z_2_n));  // open: nQ
  D_FF #(.Default(1)) u_Z_1_n (.D(or_5_out), .C(C), .Q(Z_1_n));  // open: nQ
  D_FF u_Z_0_n (.D(or_6_out), .C(C), .Q(Z_0_n));  // open: nQ
  // Probe serpent_basic.fsm on {U, D, Z_5_n, Z_4_n, Z_3_n, Z_2_n, Z_1_n, Z_0_n}

  // Notes on the sheet:
  //   C: Hz: 2
endmodule
