// Digital circuit serpent_avec_control_ameliore_AFF7SEG.dig as structural Verilog
module serpent_avec_control_ameliore_AFF7SEG (
  input  clk
);

  wire BAS_out, CENTRE_out, DROITE_out, GAUCHE_out, HAUT_out, not_1_out, not_2_out, not_3_out, not_4_out,
       serpent_avec_control_ameliore_basys3_1_an0, serpent_avec_control_ameliore_basys3_1_an1,
       serpent_avec_control_ameliore_basys3_1_an2, serpent_avec_control_ameliore_basys3_1_an3,
       serpent_avec_control_ameliore_basys3_1_ca, serpent_avec_control_ameliore_basys3_1_cb,
       serpent_avec_control_ameliore_basys3_1_cc, serpent_avec_control_ameliore_basys3_1_cd,
       serpent_avec_control_ameliore_basys3_1_ce, serpent_avec_control_ameliore_basys3_1_cf,
       serpent_avec_control_ameliore_basys3_1_cg;

  Button CENTRE (.out(CENTRE_out));
  Button HAUT (.out(HAUT_out));
  Button BAS (.out(BAS_out));
  Button DROITE (.out(DROITE_out));
  Button GAUCHE (.out(GAUCHE_out));
  serpent_avec_control_ameliore_BASYS3 serpent_avec_control_ameliore_basys3_1 (
    .Clock(clk), .Center(CENTRE_out), .Up(HAUT_out), .Down(BAS_out), .Right(DROITE_out), .Left(GAUCHE_out),
    .AN3(serpent_avec_control_ameliore_basys3_1_an3), .AN2(serpent_avec_control_ameliore_basys3_1_an2),
    .AN1(serpent_avec_control_ameliore_basys3_1_an1), .AN0(serpent_avec_control_ameliore_basys3_1_an0),
    .CD(serpent_avec_control_ameliore_basys3_1_cd), .CC(serpent_avec_control_ameliore_basys3_1_cc),
    .CB(serpent_avec_control_ameliore_basys3_1_cb), .CA(serpent_avec_control_ameliore_basys3_1_ca),
    .CE(serpent_avec_control_ameliore_basys3_1_ce), .CF(serpent_avec_control_ameliore_basys3_1_cf),
    .CG(serpent_avec_control_ameliore_basys3_1_cg));
  Seven_Seg #(.commonCathode("true"), .commonConnectionType("anode")) seven_seg_1 (
    .a(serpent_avec_control_ameliore_basys3_1_ca), .b(serpent_avec_control_ameliore_basys3_1_cb),
    .c(serpent_avec_control_ameliore_basys3_1_cc), .d(serpent_avec_control_ameliore_basys3_1_cd),
    .e(serpent_avec_control_ameliore_basys3_1_ce), .f(serpent_avec_control_ameliore_basys3_1_cf),
    .g(serpent_avec_control_ameliore_basys3_1_cg), .dp(1'b1), .common(not_1_out));
  not not_1 (not_1_out, serpent_avec_control_ameliore_basys3_1_an3);
  Seven_Seg #(.commonCathode("true"), .commonConnectionType("anode")) seven_seg_2 (
    .a(serpent_avec_control_ameliore_basys3_1_ca), .b(serpent_avec_control_ameliore_basys3_1_cb),
    .c(serpent_avec_control_ameliore_basys3_1_cc), .d(serpent_avec_control_ameliore_basys3_1_cd),
    .e(serpent_avec_control_ameliore_basys3_1_ce), .f(serpent_avec_control_ameliore_basys3_1_cf),
    .g(serpent_avec_control_ameliore_basys3_1_cg), .dp(1'b1), .common(not_2_out));
  not not_2 (not_2_out, serpent_avec_control_ameliore_basys3_1_an2);
  Seven_Seg #(.commonCathode("true"), .commonConnectionType("anode")) seven_seg_3 (
    .a(serpent_avec_control_ameliore_basys3_1_ca), .b(serpent_avec_control_ameliore_basys3_1_cb),
    .c(serpent_avec_control_ameliore_basys3_1_cc), .d(serpent_avec_control_ameliore_basys3_1_cd),
    .e(serpent_avec_control_ameliore_basys3_1_ce), .f(serpent_avec_control_ameliore_basys3_1_cf),
    .g(serpent_avec_control_ameliore_basys3_1_cg), .dp(1'b1), .common(not_3_out));
  not not_3 (not_3_out, serpent_avec_control_ameliore_basys3_1_an1);
  Seven_Seg #(.commonCathode("true"), .commonConnectionType("anode")) seven_seg_4 (
    .a(serpent_avec_control_ameliore_basys3_1_ca), .b(serpent_avec_control_ameliore_basys3_1_cb),
    .c(serpent_avec_control_ameliore_basys3_1_cc), .d(serpent_avec_control_ameliore_basys3_1_cd),
    .e(serpent_avec_control_ameliore_basys3_1_ce), .f(serpent_avec_control_ameliore_basys3_1_cf),
    .g(serpent_avec_control_ameliore_basys3_1_cg), .dp(1'b1), .common(not_4_out));
  not not_4 (not_4_out, serpent_avec_control_ameliore_basys3_1_an0);

  // Notes on the sheet:
  //   clk: Hz: 5
endmodule
