// Digital circuit serpent_avec_control_ameliore_BASYS3.dig as structural Verilog
module serpent_avec_control_ameliore_BASYS3 (
  input  Clock,
  input  Center,
  input  Up,
  input  Down,
  input  Right,
  input  Left,
  output AN3,
  output AN2,
  output AN1,
  output AN0,
  output CD,
  output CC,
  output CB,
  output CA,
  output CE,
  output CF,
  output CG
);

  wire or_1_out, or_2_out, or_3_out, or_4_out, or_5_out, or_6_out, or_7_out, or_8_out, or_9_out, or_10_out,
       or_11_out;

  not not_1 (AN3, or_1_out);
  // Or or_1 has open pins: In_1=open, In_2=open, In_3=open, In_4=open, In_5=open, In_6=open, In_7=open, out=or_1_out
  not not_2 (AN2, or_2_out);
  // Or or_2 has open pins: In_1=open, In_2=open, In_3=open, In_4=open, In_5=open, In_6=open, In_7=open, out=or_2_out
  not not_3 (AN1, or_3_out);
  // Or or_3 has open pins: In_1=open, In_2=open, In_3=open, In_4=open, In_5=open, In_6=open, In_7=open, out=or_3_out
  // Or or_4 has open pins: In_1=open, In_2=open, In_3=open, In_4=open, In_5=open, In_6=open, In_7=open, out=or_4_out
  not not_4 (AN0, or_4_out);
  // Or or_5 has open pins: In_1=open, In_2=open, In_3=open, In_4=open, In_5=open, In_6=open, In_7=open, out=or_5_out
  not not_5 (CA, or_5_out);
  not not_6 (CB, or_6_out);
  // Or or_6 has open pins: In_1=open, In_2=open, In_3=open, In_4=open, In_5=open, In_6=open, In_7=open, out=or_6_out
  not not_7 (CC, or_7_out);
  // Or or_7 has open pins: In_1=open, In_2=open, In_3=open, In_4=open, In_5=open, In_6=open, In_7=open, out=or_7_out
  not not_8 (CD, or_8_out);
  // Or or_8 has open pins: In_1=open, In_2=open, In_3=open, In_4=open, In_5=open, In_6=open, In_7=open, out=or_8_out
  // Or or_9 has open pins: In_1=open, In_2=open, In_3=open, In_4=open, In_5=open, In_6=open, In_7=open, out=or_9_out
  not not_9 (CE, or_9_out);
  not not_10 (CF, or_10_out);
  // Or or_10 has open pins: In_1=open, In_2=open, In_3=open, In_4=open, In_5=open, In_6=open, In_7=open, out=or_10_out
  not not_11 (CG, or_11_out);
  // Or or_11 has open pins: In_1=open, In_2=open, In_3=open, In_4=open, In_5=open, In_6=open, In_7=open, out=or_11_out

  // Notes on the sheet:
  //   Clock: pin W5, Hz: 5
  //   AN3: pin W4
  //   AN2: pin V4
  //   AN1: pin U4
  //   AN0: pin U2
  //   CD: pin V8
  //   CC: pin U8
  //   CB: pin W6
  //   CA: pin W7
  //   CE: pin U5
  //   CF: pin V5
  //   CG: pin U7
  //   Center: pin U18
  //   Up: pin T18
  //   Down: pin U17
  //   Right: pin T17
  //   Left: pin W19
endmodule
