// Digital circuit serpent_basic.dig as structural Verilog
module serpent_basic (
  input  C,
  output A00,
  output A01,
  output A02,
  output A03,
  output A10,
  output A13,
  output A20,
  output A23,
  output A30,
  output A33,
  output A34,
  output A35
);

  wire and_1_out, and_2_out, and_3_out, and_4_out, and_5_out, and_6_out, and_7_out, and_8_out, not_1_out,
       not_2_out, not_3_out, not_4_out, or_1_out, or_2_out, or_3_out, Z_0_n, Z_1_n, Z_2_n, Z_3_n;

  not not_1 (not_1_out, Z_3_n);
  not not_2 (not_2_out, Z_2_n);
  not not_3 (not_3_out, Z_1_n);
  not not_4 (not_4_out, Z_0_n);
  and and_1 (and_1_out, Z_0_n, Z_1_n, Z_2_n);
  and and_2 (and_2_out, not_4_out, Z_3_n);
  and and_3 (and_3_out, not_3_out, Z_3_n);
  and and_4 (and_4_out, Z_0_n, Z_1_n, not_2_out, not_1_out);
  and and_5 (and_5_out, not_4_out, Z_2_n);
  and and_6 (and_6_out, not_3_out, Z_2_n);
  and and_7 (and_7_out, Z_0_n, not_3_out);
  and and_8 (and_8_out, not_4_out, Z_1_n);
  and and_9 (A00, Z_0_n, Z_1_n, not_2_out, not_1_out);
  and and_10 (A01, not_4_out, not_3_out, Z_2_n);
  and and_11 (A02, Z_0_n, not_3_out, Z_2_n);
  and and_12 (A03, not_4_out, Z_1_n, Z_2_n);
  and and_13 (A10, not_4_out, Z_1_n, not_2_out, not_1_out);
  and and_14 (A13, Z_0_n, Z_1_n, Z_2_n);
  and and_15 (A20, Z_0_n, not_3_out, not_2_out, not_1_out);
  and and_16 (A23, not_4_out, not_3_out, Z_3_n);
  and and_17 (A30, not_4_out, not_3_out, not_2_out, not_1_out);
  and and_18 (A33, Z_0_n, not_3_out, Z_3_n);
  and and_19 (A34, not_4_out, Z_1_n, Z_3_n);
  and and_20 (A35, Z_0_n, Z_1_n, Z_3_n);
  or or_1 (or_1_out, and_1_out, and_2_out, and_3_out);
  or or_2 (or_2_out, and_4_out, and_5_out, and_6_out);
  or or_3 (or_3_out, and_7_out, and_8_out);
  D_FF u_Z_3_n (.D(or_1_out), .C(C), .Q(Z_3_n));  // open: nQ
  D_FF u_Z_2_n (.D(or_2_out), .C(C), .Q(Z_2_n));  // open: nQ
  D_FF u_Z_1_n (.D(or_3_out), .C(C), .Q(Z_1_n));  // open: nQ
  D_FF u_Z_0_n (.D(not_4_out), .C(C), .Q(Z_0_n));  // open: nQ
  // Probe serpent_basic.fsm on {Z_3_n, Z_2_n, Z_1_n, Z_0_n}

  // Notes on the sheet:
  //   C: Hz: 2
endmodule
