// Digital circuit serpent_basic_AFF7SEG.dig as structural Verilog
module serpent_basic_AFF7SEG (
  input  clk
);

  wire not_1_out, not_2_out, not_3_out, not_4_out, serpent_basic_basys3_1_an0, serpent_basic_basys3_1_an1,
       serpent_basic_basys3_1_an2, serpent_basic_basys3_1_an3, serpent_basic_basys3_1_ca,
       serpent_basic_basys3_1_cb, serpent_basic_basys3_1_cc, serpent_basic_basys3_1_cd,
       serpent_basic_basys3_1_ce, serpent_basic_basys3_1_cf, serpent_basic_basys3_1_cg;

  serpent_basic_BASYS3 serpent_basic_basys3_1 (
    .Clock(clk), .AN3(serpent_basic_basys3_1_an3), .AN2(serpent_basic_basys3_1_an2),
    .AN1(serpent_basic_basys3_1_an1), .AN0(serpent_basic_basys3_1_an0), .CD(serpent_basic_basys3_1_cd),
    .CC(serpent_basic_basys3_1_cc), .CB(serpent_basic_basys3_1_cb), .CA(serpent_basic_basys3_1_ca),
    .CE(serpent_basic_basys3_1_ce), .CF(serpent_basic_basys3_1_cf), .CG(serpent_basic_basys3_1_cg));
  Seven_Seg #(.commonConnectionType("anode"), .commonCathode("true")) seven_seg_1 (
    .a(serpent_basic_basys3_1_ca), .b(serpent_basic_basys3_1_cb), .c(serpent_basic_basys3_1_cc),
    .d(serpent_basic_basys3_1_cd), .e(serpent_basic_basys3_1_ce), .f(serpent_basic_basys3_1_cf),
    .g(serpent_basic_basys3_1_cg), .dp(1'b1), .common(not_1_out));
  not not_1 (not_1_out, serpent_basic_basys3_1_an3);
  Seven_Seg #(.commonCathode("true"), .commonConnectionType("anode")) seven_seg_2 (
    .a(serpent_basic_basys3_1_ca), .b(serpent_basic_basys3_1_cb), .c(serpent_basic_basys3_1_cc),
    .d(serpent_basic_basys3_1_cd), .e(serpent_basic_basys3_1_ce), .f(serpent_basic_basys3_1_cf),
    .g(serpent_basic_basys3_1_cg), .dp(1'b1), .common(not_2_out));
  not not_2 (not_2_out, serpent_basic_basys3_1_an2);
  Seven_Seg #(.commonCathode("true"), .commonConnectionType("anode")) seven_seg_3 (
    .a(serpent_basic_basys3_1_ca), .b(serpent_basic_basys3_1_cb), .c(serpent_basic_basys3_1_cc),
    .d(serpent_basic_basys3_1_cd), .e(serpent_basic_basys3_1_ce), .f(serpent_basic_basys3_1_cf),
    .g(serpent_basic_basys3_1_cg), .dp(1'b1), .common(not_3_out));
  not not_3 (not_3_out, serpent_basic_basys3_1_an1);
  Seven_Seg #(.commonCathode("true"), .commonConnectionType("anode")) seven_seg_4 (
    .a(serpent_basic_basys3_1_ca), .b(serpent_basic_basys3_1_cb), .c(serpent_basic_basys3_1_cc),
    .d(serpent_basic_basys3_1_cd), .e(serpent_basic_basys3_1_ce), .f(serpent_basic_basys3_1_cf),
    .g(serpent_basic_basys3_1_cg), .dp(1'b1), .common(not_4_out));
  not not_4 (not_4_out, serpent_basic_basys3_1_an0);

  // Notes on the sheet:
  //   clk: Hz: 5
endmodule
