// Digital circuit serpent_basic_BASYS3.dig as structural Verilog
module serpent_basic_BASYS3 (
  input  Clock,
  output AN3,
  output AN2,
  output AN1,
  output AN0,
  output CD,
  output CC,
  output CB,
  output CA,
  output CE,
  output CF,
  output CG
);

  wire or_1_out, or_2_out, or_3_out, or_4_out, or_5_out, or_6_out, or_7_out, or_8_out, or_9_out, or_10_out,
       or_11_out, serpent_basic_1_a00, serpent_basic_1_a01, serpent_basic_1_a02, serpent_basic_1_a03,
       serpent_basic_1_a10, serpent_basic_1_a13, serpent_basic_1_a20, serpent_basic_1_a23,
       serpent_basic_1_a30, serpent_basic_1_a33, serpent_basic_1_a34, serpent_basic_1_a35;

  serpent_basic serpent_basic_1 (
    .C(Clock), .A00(serpent_basic_1_a00), .A01(serpent_basic_1_a01), .A02(serpent_basic_1_a02),
    .A03(serpent_basic_1_a03), .A10(serpent_basic_1_a10), .A13(serpent_basic_1_a13),
    .A20(serpent_basic_1_a20), .A23(serpent_basic_1_a23), .A30(serpent_basic_1_a30),
    .A33(serpent_basic_1_a33), .A34(serpent_basic_1_a34), .A35(serpent_basic_1_a35));
  not not_1 (AN0, or_1_out);
  or or_1 (or_1_out, 1'b0, 1'b0, 1'b0, serpent_basic_1_a03, serpent_basic_1_a02, serpent_basic_1_a01, serpent_basic_1_a00);
  not not_2 (AN1, or_2_out);
  or or_2 (or_2_out, 1'b0, 1'b0, 1'b0, 1'b0, 1'b0, serpent_basic_1_a13, serpent_basic_1_a10);
  not not_3 (AN2, or_3_out);
  or or_3 (or_3_out, 1'b0, 1'b0, 1'b0, 1'b0, 1'b0, serpent_basic_1_a23, serpent_basic_1_a20);
  or or_4 (or_4_out, 1'b0, 1'b0, 1'b0, serpent_basic_1_a35, serpent_basic_1_a34, serpent_basic_1_a33, serpent_basic_1_a30);
  not not_4 (AN3, or_4_out);
  or or_5 (or_5_out, 1'b0, 1'b0, 1'b0, serpent_basic_1_a30, serpent_basic_1_a20, serpent_basic_1_a10, serpent_basic_1_a00);
  not not_5 (CA, or_5_out);
  not not_6 (CB, or_6_out);
  or or_6 (or_6_out, 1'b0, 1'b0, 1'b0, 1'b0, 1'b0, 1'b0, serpent_basic_1_a01);
  not not_7 (CC, or_7_out);
  or or_7 (or_7_out, 1'b0, 1'b0, 1'b0, 1'b0, 1'b0, 1'b0, serpent_basic_1_a02);
  not not_8 (CD, or_8_out);
  or or_8 (or_8_out, 1'b0, 1'b0, 1'b0, serpent_basic_1_a33, serpent_basic_1_a23, serpent_basic_1_a13, serpent_basic_1_a03);
  or or_9 (or_9_out, 1'b0, 1'b0, 1'b0, 1'b0, 1'b0, 1'b0, serpent_basic_1_a34);
  not not_9 (CE, or_9_out);
  not not_10 (CF, or_10_out);
  or or_10 (or_10_out, 1'b0, 1'b0, 1'b0, 1'b0, 1'b0, 1'b0, serpent_basic_1_a35);
  not not_11 (CG, or_11_out);
  or or_11 (or_11_out, 1'b0, 1'b0, 1'b0, 1'b0, 1'b0, 1'b0, 1'b0);

  // Notes on the sheet:
  //   Clock: pin W5
  //   AN3: pin W4
  //   AN2: pin V4
  //   AN1: pin U4
  //   AN0: pin U2
  //   CD: pin V8
  //   CC: pin U8
  //   CB: pin W6
  //   CA: pin W7
  //   CE: pin U5
  //   CF: pin V5
  //   CG: pin U7
endmodule
